# Fritzing sketch SLAVE_HW_DESIGN (saved by Fritzing 0.9.3b)
breadboards: 1

parts:
  Part1 = Arduino Pro Mini (5V)
  U1 = MAX485 [package=dil08]
  J1 = screw terminal, 3 pins
  R2 = Resistor [tolerance=±5% resistance=10k package="0805 [SMD]"]
  R3 = Resistor [tolerance=±5% resistance=10k package="0805 [SMD]"]
  R4 = Resistor [tolerance=±5% resistance=10k package="0805 [SMD]"]
  R5 = Resistor [tolerance=±5% resistance=10k package="0805 [SMD]"]
  R6 = Resistor [tolerance=±5% resistance=22k package="0805 [SMD]"]
  R7 = Resistor [tolerance=±5% resistance=22k package="0805 [SMD]"]
  R8 = Resistor [tolerance=±5% resistance=100 package="0805 [SMD]"]
  J2 = screw terminal, 3 pins

nets:
  N1: Part1.D3, U1.DE, R3.Pin_0
  N2: Part1.D2, U1.RE, R5.Pin_0
  N3: Part1.RXI, U1.DI, R4.Pin_0
  N4: Part1.TXO, U1.RO, R2.Pin_0
  N5: U1.GND, J1.pin3, R7.Pin_1, J2.pin3
  N6: U1.A, J1.pin1, R6.Pin_1, R8.Pin_1, J2.pin1
  N7: U1.B, J1.pin2, R7.Pin_0, R8.Pin_0, J2.pin2
  N8: U1.VCC, R2.Pin_1, R3.Pin_1, R4.Pin_1, R5.Pin_1, R6.Pin_0
